# Fritzing sketch DACN (saved by Fritzing 0.9.3b)

parts:
  U2 = NodeMCU V1.0
  LoRa_Module1 = Ra-01 - LoRa Module SX1278 [part_number=SX1278]

nets:
  N1: U2.D0, LoRa_Module1.RESET
  N2: U2.D4, LoRa_Module1.DIO0
  N3: U2.D5, LoRa_Module1.SCK
  N4: U2.D6, LoRa_Module1.MISO
  N5: U2.D7, LoRa_Module1.MOSI
  N6: U2.D8, LoRa_Module1.NSS
  GND: U2.GND, LoRa_Module1.GND
  3V3: U2.3V3, LoRa_Module1.3.3V

custom parts:
  NodeMCU V1.0: ESP8266 based NodeMCU
  Ra-01 - LoRa Module SX1278: The Ra-01 LoRa Module featuring the SX1278 engine by Semtech. Module by AI-Thinker. Module (Ra-01) specifications from: https://www.banggood.com/Ra-01-Smart-Electronics-SX1278-LoRa-Spread-Spectrum-Wireless-Module-Ultra-Far-10KM-433M-p-1130769.html Description: Power supply: DC1.8-3.7V(3.3V) Chip: SX1278 Frequency: 433Mhz Operating temperature: -40~+85°C On Sheild Description (may vary by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
