# Fritzing sketch lora (saved by Fritzing 0.9.3b)

parts:
  U1 = NodeMCU V1.0
  DHT11_1 = DHT11 module
  M1 = Osoyoo SX1278-ra-02
  Part1 = FC-28 Soil Hygrometer Module - Probe
  Part2 = FC-28 Soil Hygrometer Module
  Part3 = FC-28 Soil Hygrometer Module

nets:
  N1: U1.D0, M1.RST
  N2: U1.D1, M1.DIO0
  N3: U1.D3, DHT11_1.DATA
  N4: U1.D4, Part2.DO
  VCC: U1.3V3, U1.D8, DHT11_1.VCC, M1.3.3V, M1.DIO1, M1.NSS, Part2.VCC, Part3.VCC
  GND: U1.GND, DHT11_1.GND, M1.GND, Part2.GND, Part3.GND
  N5: U1.D5, M1.SCK
  N6: U1.D6, M1.MISO
  N7: U1.D7, M1.MOSI
  N8: U1.A0, Part3.AO
  N9: Part1.POS, Part3.POS
  N10: Part1.NEG, Part3.NEG

custom parts:
  NodeMCU V1.0: ESP8266 based NodeMCU
  DHT11 module: https://cdn-learn.adafruit.com/downloads/pdf/dht.pdf DHT11 black pcb module reference by:https://github.com/adafruit/Fritzing-Library/blob/master/parts/DHT11%20Humitidy%20and%20Temperature%20Sensor.fzpz
  Osoyoo SX1278-ra-02: Osoyoo Long Distance wireless transceiver Uart LoRa Module.
  FC-28 Soil Hygrometer Module - Probe: The FC-28 is a soil hygrometer module that uses the Texas Instruments LM393 comparator chip to provide an analog measurement of soil humidity.
  FC-28 Soil Hygrometer Module: The FC-28 is a soil hygrometer module that uses the Texas Instruments LM393 comparator chip to provide an analog measurement of soil humidity. The digital output is high when soil moisture is over a certain threshold, as determined by adjusting the potentiometer.
